# Fritzing sketch circuito - monitoramento (saved by Fritzing 0.9.3b)
breadboards: 1

parts:
  LED1 = LED - 5mm [color="Blue (430nm)" package="5 mm [THT]"]
  Componente2 = Soil Moisture Sensor
  DHT1 = DHT11 Humitidy and Temperature Sensor
  Display1 = LCD screen 16x2 IIC [part_number=101290]
  R1 = Resistor [tolerance=±5% resistance=220 package="0603 [SMD]"]
  Componente1 = Arduino Uno (Rev3)

nets:
  N1: LED1.cathode, Componente1.D7
  N2: LED1.anode, R1.Pin_0
  VCC: Componente2.VCC, DHT1.VDD, Display1.VCC, Componente1.5V
  GND: Componente2.GND, DHT1.GND, Display1.GND, R1.Pin_1
  N3: Componente2.SIG, Componente1.A0
  N4: DHT1.DATA, Componente1.A1
  N5: Display1.SDA, Componente1.A4/SDA
  N6: Display1.SCL, Componente1.A5/SCL

custom parts:
  DHT11 Humitidy and Temperature Sensor: DHT11 Humidity and Temperature Sensor
  LCD screen 16x2 IIC: LCD screen with HD44780 controller enables showing text, symbols, value or anything else that comes from Croduino/Arduino. It is capable of showing 16 symbols in two lines and therefore can be used in many projects that need to send clearly visible and legible output information.. • Color of symbols: White • Backlight: Blue • Dimensions: 80 x 36 x 12 mm • Screen dimensions: 64.5 x 16 mm •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
